// Logisim project Circuito Exercicio 1.circ as structural Verilog: 1 circuit, main circuit main
module main (
  input  A,
  input  B,
  input  C,
  input  D,
  output W,
  output X,
  output Y,
  output Z
);

  wire and_1_out, and_2_out, and_3_out, and_4_out, nor_1_out, nor_2_out, nor_3_out, or_1_out, or_2_out,
       or_3_out, or_4_out, xor_1_out;

  xor xor_1 (xor_1_out, A, D);
  or or_1 (or_1_out, A, C);
  nor nor_1 (nor_1_out, A, C);
  and and_1 (and_1_out, B, D);
  nor nor_2 (nor_2_out, C, D);
  nor nor_3 (nor_3_out, B, D);
  or or_2 (or_2_out, B, ~D);  // OR_Gate
  or or_3 (or_3_out, xor_1_out, C);
  and and_2 (and_2_out, or_1_out, D);
  or or_4 (or_4_out, nor_1_out, B);
  and and_3 (and_3_out, or_4_out, ~D);  // AND_Gate
  or or_5 (Y, and_1_out, nor_2_out);
  and and_4 (and_4_out, or_2_out, C);
  or or_6 (W, or_3_out, B);
  or or_7 (X, and_2_out, and_3_out);
  or or_8 (Z, nor_3_out, and_4_out, A);
endmodule
