// Logisim project Circuito Exercicio 2.circ as structural Verilog: 2 circuits, main circuit main
module main (
  input  A,
  input  B,
  input  I,
  output S
);

  Circuito_Exercicio_2 circuito_exercicio_2_1 (.A(A), .B(B), .I(I), .S(S));
endmodule

module Circuito_Exercicio_2 (
  input  A,
  input  B,
  input  I,
  output S
);

  wire and_1_out, and_2_out;

  and and_1 (and_1_out, ~A, ~I);  // AND_Gate
  and and_2 (and_2_out, ~B, I);  // AND_Gate
  or or_1 (S, and_1_out, and_2_out);
endmodule
