// Logisim project Circuito Exercicio 3.circ as structural Verilog: 1 circuit, main circuit main
module main (
  input  A,
  input  B,
  input  C,
  input  D,
  output S1,
  output S2,
  output S3,
  output S4,
  output S5
);

  wire and_1_out, and_2_out, and_3_out, and_4_out, and_5_out, nor_1_out, or_1_out, xor_1_out, xor_2_out;

  nor nor_1 (nor_1_out, A, C);
  xor xor_1 (xor_1_out, B, C);
  and and_1 (and_1_out, C, ~D);  // AND_Gate
  xor xor_2 (xor_2_out, B, C);
  and and_2 (and_2_out, C, D);
  and and_3 (and_3_out, A, ~D);  // AND_Gate
  or or_1 (or_1_out, C, D);
  and and_4 (and_4_out, nor_1_out, D);
  or or_2 (S2, and_1_out, xor_2_out);
  or or_3 (S3, and_2_out, B);
  or or_4 (S4, and_3_out, B);
  and and_5 (and_5_out, or_1_out, B);
  or or_5 (S5, and_5_out, A);
  or or_6 (S1, and_4_out, xor_1_out);
endmodule
