// Logisim project Circuito Exercicio 4.circ as structural Verilog: 2 circuits, main circuit main
module main (
  input  in_1,
  input  in_2,
  input  in_3
);

  wire circuito_exercicio_4_1_a_2, circuito_exercicio_4_1_b_2, circuito_exercicio_4_1_c_2,
       circuito_exercicio_4_1_d, circuito_exercicio_4_1_e, circuito_exercicio_4_1_f, circuito_exercicio_4_1_g;

  Circuito_Exercicio_4 circuito_exercicio_4_1 (
    .A(in_1), .B(in_2), .C(in_3), .a_2(circuito_exercicio_4_1_a_2), .b_2(circuito_exercicio_4_1_b_2),
    .c_2(circuito_exercicio_4_1_c_2), .d(circuito_exercicio_4_1_d), .e(circuito_exercicio_4_1_e),
    .f(circuito_exercicio_4_1_f), .g(circuito_exercicio_4_1_g));
  _7_Segment_Display u_7_segment_display_1 (
    .g(circuito_exercicio_4_1_g), .f(circuito_exercicio_4_1_f), .a(circuito_exercicio_4_1_a_2),
    .b(circuito_exercicio_4_1_b_2), .e(circuito_exercicio_4_1_e), .d(circuito_exercicio_4_1_d),
    .c(circuito_exercicio_4_1_c_2));  // open: dp
endmodule

module Circuito_Exercicio_4 (
  input  A,
  input  B,
  input  C,
  output a_2,
  output b_2,
  output c_2,
  output d,
  output e,
  output f,
  output g
);

  wire nor_1_out, not_1_out, not_2_out, not_3_out, not_4_out;

  not not_1 (not_1_out, C);
  not not_2 (not_2_out, C);
  or or_1 (d, A, C);
  not not_3 (not_3_out, B);
  not not_4 (not_4_out, B);
  or or_2 (a_2, C, nor_1_out);
  nor nor_1 (nor_1_out, A, B);
  or or_3 (b_2, A, B, not_1_out);
  or or_4 (c_2, A, B, not_2_out);
  or or_5 (e, A, not_3_out, C);
  or or_6 (f, A, not_4_out, C);
  nor nor_2 (g, A, B);
endmodule
