// Logisim project Circuito Exercicio 5.circ as structural Verilog: 2 circuits, main circuit main
module main (
  input  A,
  input  B,
  input  C
);

  wire circuito_exercicio_5_1_l1, circuito_exercicio_5_1_l2, circuito_exercicio_5_1_l3,
       circuito_exercicio_5_1_l4, circuito_exercicio_5_1_l5, circuito_exercicio_5_1_l6,
       circuito_exercicio_5_1_l7;

  LED led_1 (.in(circuito_exercicio_5_1_l1));
  LED led_2 (.in(circuito_exercicio_5_1_l5));
  LED led_3 (.in(circuito_exercicio_5_1_l2));
  LED led_4 (.in(circuito_exercicio_5_1_l4));
  LED led_5 (.in(circuito_exercicio_5_1_l3));
  Circuito_Exercicio_5 circuito_exercicio_5_1 (
    .A(A), .B(B), .C(C), .L1(circuito_exercicio_5_1_l1), .L2(circuito_exercicio_5_1_l2),
    .L3(circuito_exercicio_5_1_l3), .L4(circuito_exercicio_5_1_l4), .L5(circuito_exercicio_5_1_l5),
    .L6(circuito_exercicio_5_1_l6), .L7(circuito_exercicio_5_1_l7));
  LED led_6 (.in(circuito_exercicio_5_1_l7));
  LED led_7 (.in(circuito_exercicio_5_1_l6));
endmodule

module Circuito_Exercicio_5 (
  input  A,
  input  B,
  input  C,
  output L1,
  output L2,
  output L3,
  output L4,
  output L5,
  output L6,
  output L7
);

  wire and_1_out, or_3_out;

  or or_1 (L1, A, B, C);
  or or_2 (L2, A, B);
  and and_1 (and_1_out, B, C);
  or or_3 (or_3_out, B, C);
  and and_2 (L6, A, B);
  and and_3 (L7, A, B, C);
  or or_4 (L3, A, and_1_out);
  and and_4 (L5, A, or_3_out);

  assign L4 = A;
endmodule
