// Logisim project Circuito Exercicio 6.circ as structural Verilog: 2 circuits, main circuit main
module main (
  input  A,
  input  B,
  input  C,
  input  D,
  output S3,
  output S2,
  output S1,
  output S0
);

  Circuito_Exercicio_6 circuito_exercicio_6_1 (.A(A), .B(B), .C(C), .D(D), .S3(S3), .S2(S2), .S1(S1), .S0(S0));
endmodule

module Circuito_Exercicio_6 (
  input  A,
  input  B,
  input  C,
  input  D,
  output S3,
  output S2,
  output S1,
  output S0
);

  or or_1 (S2, A, B);
  xor xor_1 (S1, B, C);
  xor xor_2 (S0, C, D);

  assign S3 = A;
endmodule
