// Logisim project Circuito Exercicio 7.circ as structural Verilog: 2 circuits, main circuit main
module main (
  input  A,
  input  B,
  input  C,
  output S
);

  Circuito_Exercicio_7 circuito_exercicio_7_1 (.A(A), .B(B), .C(C), .S(S));
endmodule

module Circuito_Exercicio_7 (
  input  A,
  input  B,
  input  C,
  output S
);

  wire and_1_out, and_2_out, xnor_1_out, xor_1_out;

  xnor xnor_1 (xnor_1_out, B, C);
  xor xor_1 (xor_1_out, C, B);
  and and_1 (and_1_out, xnor_1_out, ~A);  // AND_Gate
  and and_2 (and_2_out, xor_1_out, A);
  or or_1 (S, and_1_out, and_2_out);
endmodule
