// Logisim project Circuito Exercicio 8.circ as structural Verilog: 2 circuits, main circuit main
module main (
  input  A,
  input  B,
  input  C,
  input  D,
  output S3,
  output S2,
  output S1,
  output S0
);

  Circuito_Exercicio_8 circuito_exercicio_8_1 (.A(A), .B(B), .C(C), .D(D), .S3(S3), .S2(S2), .S1(S1), .S0(S0));
endmodule

module Circuito_Exercicio_8 (
  input  A,
  input  B,
  input  C,
  input  D,
  output S3,
  output S2,
  output S1,
  output S0
);

  wire and_2_out, and_3_out, and_4_out, and_5_out, and_7_out, and_8_out, nand_1_out, nand_2_out, or_1_out;

  and and_1 (S3, A, B, C, D);
  and and_2 (and_2_out, A, ~B);  // AND_Gate
  and and_3 (and_3_out, A, ~D);  // AND_Gate
  and and_4 (and_4_out, B, C);
  nand nand_1 (nand_1_out, A, D);
  and and_5 (and_5_out, A, D);
  nand nand_2 (nand_2_out, B, C);
  and and_6 (S0, B, D);
  or or_1 (or_1_out, and_2_out, and_3_out);
  and and_7 (and_7_out, and_4_out, nand_1_out);
  and and_8 (and_8_out, and_5_out, nand_2_out);
  and and_9 (S2, or_1_out, C);
  or or_2 (S1, and_7_out, and_8_out);
endmodule
