// Logisim project CircuitoMotor.circ as structural Verilog: 2 circuits, main circuit main
module main (
  input  A,
  input  B,
  input  C,
  output P1,
  output P2,
  output P3,
  output P4,
  output P5,
  output P6,
  output P7,
  output P8
);

  wire and_3_out, and_4_out, and_7_out, and_8_out, xor_1_out, xor_2_out;

  and and_1 (P1, ~A, ~B);  // AND_Gate
  and and_2 (P3, ~A, B);  // AND_Gate
  and and_3 (and_3_out, ~A, B, C);  // AND_Gate
  and and_4 (and_4_out, A, ~B, ~C);  // AND_Gate
  and and_5 (P5, A, ~B);  // AND_Gate
  xor xor_1 (xor_1_out, B, C);
  and and_6 (P7, A, B);
  and and_7 (and_7_out, A, B, C);
  and and_8 (and_8_out, ~A, ~B, ~C);  // AND_Gate
  and and_9 (P2, ~A, xor_2_out);  // AND_Gate
  xor xor_2 (xor_2_out, B, C);
  or or_1 (P4, and_3_out, and_4_out);
  and and_10 (P6, A, xor_1_out);
  or or_2 (P8, and_7_out, and_8_out);
endmodule

module ExercicioCircuito (
  input  in_1,
  input  in_2,
  input  in_3
);

  wire main_1_p1, main_1_p2, main_1_p3, main_1_p4, main_1_p5, main_1_p6, main_1_p7, main_1_p8;

  main main_1 (
    .P1(main_1_p1), .P2(main_1_p2), .P3(main_1_p3), .P4(main_1_p4), .P5(main_1_p5), .P6(main_1_p6),
    .P7(main_1_p7), .P8(main_1_p8), .A(in_1), .B(in_2), .C(in_3));
  LED led_1 (.in(main_1_p1));
  LED led_2 (.in(main_1_p2));
  LED led_3 (.in(main_1_p3));
  LED led_4 (.in(main_1_p4));
  LED led_5 (.in(main_1_p5));
  LED led_6 (.in(main_1_p6));
  LED led_7 (.in(main_1_p7));
  LED led_8 (.in(main_1_p8));
endmodule
